# Fritzing sketch HID-Joystick (saved by Fritzing 0.9.6b)
circuit board: 6.52091cm x 3.98261cm
breadboards: 1

parts:
  Pro_Micro_5V = Arduino Pro Micro (Clone)
  S2 = Pushbutton [package="[THT]"]
  S3 = Pushbutton [package="[THT]"]
  Joystick = Thumb Joystick
  R1 = Resistor [tolerance=±5% power=0.25 resistance=10k package=THT]
  R2 = Resistor [tolerance=±5% power=0.25 resistance=10k package=THT]
  R3 = Resistor [tolerance=±5% power=0.25 resistance=10k package=THT]

nets:
  GND: Pro_Micro_5V.GND, Joystick.GND, R1.Pin_1, R2.Pin_1
  N1: Pro_Micro_5V.D2, S2.Pin_1, S2.Pin_2, R1.Pin_0
  N2: Pro_Micro_5V.D3, S3.Pin_1, S3.Pin_2, R2.Pin_0
  N3: Pro_Micro_5V.D4, Joystick.SEL, R3.Pin_1
  N4: Pro_Micro_5V.A0, Joystick.HORZ
  N5: Pro_Micro_5V.A1, Joystick.VERT
  VCC: Pro_Micro_5V.VCC, S2.Pin_3, S2.Pin_4, S3.Pin_3, S3.Pin_4, Joystick.VCC, R3.Pin_0
